# Fritzing sketch Schema_Progetto (saved by Fritzing 0.8.7b)
breadboards: 1

parts:
  U2 = 74HC595 [package="DIP16 [THT]"]
  U3 = 7-SEGMENT-DISPLAY-1_-RED [package=7-segment-1_pth]
  Arduino_UNO = Arduino Uno (Rev3)
  R1 = Resistor [tolerance=±5% resistance=100 package=THT]
  R2 = Resistor [tolerance=±5% resistance=100 package=THT]

nets:
  N1: U2.Q1, U3.B
  N2: U2.Q2, U3.C
  N3: U2.Q3, U3.D
  N4: U2.Q4, U3.E
  N5: U2.Q5, U3.F
  N6: U2.Q6, U3.G
  N7: U2.Q7, U3.A
  GND: U2.GND, U2.OE, Arduino_UNO.GND, R1.Pin_1, R2.Pin_1
  VCC: U2.MR, U2.VCC, Arduino_UNO.5V
  N8: U2.SH_CP, Arduino_UNO.D6_PWM
  N9: U2.ST_CP, Arduino_UNO.D5_PWM
  N10: U2.DS, Arduino_UNO.D4
  N11: U3.G1, R2.Pin_0
  N12: U3.G2, R1.Pin_0
